# Fritzing sketch home-alarm-board-design (saved by Fritzing 0.9.10b)
perfboards: 1

parts:
  U1 = ESP32S-HiLetgo [part_number=ESP32S-HiLetgo]
  R_pir1_10k = Resistor [tolerance=±5% power=0.25 resistance=10k package=THT]
  R_pir2_10k = Resistor [tolerance=±5% power=0.25 resistance=10k package=THT]
  R_pir3_10k = Resistor [tolerance=±5% power=0.25 resistance=10k package=THT]
  R_prox_1k = Resistor [tolerance=±5% power=0.25 resistance=1k package=THT]
  R_prox_1k4 = Resistor [tolerance=±5% power=0.25 resistance=1k package=THT]
  R_prox_1k3 = Resistor [tolerance=±5% power=0.25 resistance=1k package=THT]
  R_prox_1k2 = Resistor [tolerance=±5% power=0.25 resistance=1k package=THT]
  R_prox_1k1 = Resistor [tolerance=±5% power=0.25 resistance=1k package=THT]
  R_prox_1k5 = Resistor [tolerance=±5% power=0.25 resistance=1k package=THT]  # not connected
  R_pir3_10k1 = Resistor [tolerance=±5% power=0.25 resistance=10k package=THT]  # not connected
  J1 = Screw terminal - 2 pins [package=THT]
  J2 = Screw terminal - 2 pins [package=THT]
  J3 = Screw terminal - 2 pins [package=THT]
  J4 = Screw terminal - 2 pins [package=THT]
  J5 = Screw terminal - 2 pins [package=THT]
  J6 = Screw terminal - 2 pins [package=THT]
  J7 = Screw terminal - 2 pins [package=THT]
  J8 = Screw terminal - 2 pins [package=THT]

nets:
  N1: U1.3.3, R_pir1_10k.Pin_0, R_pir2_10k.Pin_0, R_pir3_10k.Pin_0, R_prox_1k.Pin_0, R_prox_1k4.Pin_0, R_prox_1k3.Pin_0, R_prox_1k2.Pin_0, R_prox_1k1.Pin_0
  N2: U1.GPIO36, R_pir3_10k.Pin_1, J5.pin2
  N3: U1.GPIO35, R_pir2_10k.Pin_1, J6.pin2
  N4: U1.GPIO33, R_pir1_10k.Pin_1, J7.pin2
  N5: U1.GND, J1.pin1, J2.pin2, J3.pin1, J4.pin2, J5.pin1, J6.pin1, J7.pin1, J8.pin2
  N6: U1.GPIO13, R_prox_1k.Pin_1, J8.pin1
  N7: U1.GPIO15, R_prox_1k4.Pin_1, J4.pin1
  N8: U1.GPIO4, R_prox_1k3.Pin_1, J3.pin2
  N9: U1.GPIO21, R_prox_1k2.Pin_1, J2.pin1
  N10: U1.GPIO23, R_prox_1k1.Pin_1, J1.pin2

notes:
  26x30 pin
  PROX5 (GPIO13)
  PIR1 (GPIO33)
  PIR2 (GPIO35)
  PIR3 (GPIO36)
  PROX4 (GPIO15)
  PROX3 (GPIO4)
  PROX2 (GPIO21)
  PROX1 (GPIO23)
  10kΩ
  3.3V
  signal
  1kΩ
  GND

custom parts:
  ESP32S-HiLetgo: HiLetgo ESP-WROOM-32 ESP32 ESP-32S Development Board 2.4GHz Dual-Mode WiFi + Bluetooth Dual Cores Microcontroller The ESP32 integrated with Antenna switches, RF Balun, power amplifiers, low-noise amplifiers, filters, and management modules, and the entire solution occupies the least area of PCB. 2.4 GHz Wi-Fi plus Bluetooth dual-mode chip, with TSMC Ultra-low power consumption 40nm technology,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
